# Fritzing sketch schematic_fan_control (saved by Fritzing 0.9.3b)

parts:
  U1 = attiny85 [package=dip]
  JP1 = Header 6 [package=1x06-smd]
  Raspberry_Pi_1 = Raspberry Pi 3 [part_number=RPI-3-V1.2]
  R1 = Resistor [tolerance=±5% resistance=470 package="0603 [SMD]"]
  U2 = TRANSISTOR_NPN_2 [package=to-92]
  M1 = DC Motor

nets:
  N1: U1.Pin_1, JP1.5
  N2: U1.Pin_3, R1.Pin_1
  N3: U1.Pin_4, JP1.6, Raspberry_Pi_1.GND, U2.E
  N4: U1.Pin_5, JP1.4, Raspberry_Pi_1.GPIO2
  N5: U1.Pin_6, JP1.3
  N6: U1.Pin_7, JP1.2, Raspberry_Pi_1.GPIO3
  N7: U1.Pin_8, JP1.1, Raspberry_Pi_1.3v3, M1.pin_1
  N8: R1.Pin_0, U2.B
  N9: U2.C, M1.pin_2

custom parts:
  Header 6: Header 6 Standard 6-pin 0.1 header. Use with straight break away headers (SKU : PRT-00116), right angle break away headers (PRT-00553), swiss pins (PRT-00743), machine pins (PRT-00117), and female headers (PRT-00115). Molex polarized connector foot print use with SKU : PRT-08094 with associated crimp pins and housings. NOTES ON THE VARIANTS LOCK and LOCK_LONGPADS... This footprint was designed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
